// Digital circuit ADD.dig as structural Verilog
module ADD (
  input  [31:0] RS1,
  input  [31:0] RS2,
  output Cout,
  output [31:0] S
);

  wire add_8bits_2_cout, add_8bits_3_cout, add_8bits_4_cout;

  ADD_8bits add_8bits_1 (
    .B9(RS1[24]), .B10(RS1[25]), .B11(RS1[26]), .B12(RS1[27]), .B13(RS1[28]), .B14(RS1[29]), .B15(RS1[30]),
    .B16(RS1[31]), .B1(RS2[24]), .B2(RS2[25]), .B3(RS2[26]), .B4(RS2[27]), .B5(RS2[28]), .B6(RS2[29]),
    .B7(RS2[30]), .B8(RS2[31]), .Cin(add_8bits_2_cout), .S6(S[29]), .S5(S[28]), .S4(S[27]), .S3(S[26]),
    .S2(S[25]), .S1(S[24]), .S7(S[30]), .Cout(Cout), .S8(S[31]));
  ADD_8bits add_8bits_2 (
    .B9(RS1[16]), .B10(RS1[17]), .B11(RS1[18]), .B12(RS1[19]), .B13(RS1[20]), .B14(RS1[21]), .B15(RS1[22]),
    .B16(RS1[23]), .B1(RS2[16]), .B2(RS2[17]), .B3(RS2[18]), .B4(RS2[19]), .B5(RS2[20]), .B6(RS2[21]),
    .B7(RS2[22]), .B8(RS2[23]), .Cin(add_8bits_3_cout), .S6(S[21]), .S5(S[20]), .S4(S[19]), .S3(S[18]),
    .S2(S[17]), .S1(S[16]), .S7(S[22]), .Cout(add_8bits_2_cout), .S8(S[23]));
  ADD_8bits add_8bits_3 (
    .B9(RS1[8]), .B10(RS1[9]), .B11(RS1[10]), .B12(RS1[11]), .B13(RS1[12]), .B14(RS1[13]), .B15(RS1[14]),
    .B16(RS1[15]), .B1(RS2[8]), .B2(RS2[9]), .B3(RS2[10]), .B4(RS2[11]), .B5(RS2[12]), .B6(RS2[13]),
    .B7(RS2[14]), .B8(RS2[15]), .Cin(add_8bits_4_cout), .S6(S[13]), .S5(S[12]), .S4(S[11]), .S3(S[10]),
    .S2(S[9]), .S1(S[8]), .S7(S[14]), .Cout(add_8bits_3_cout), .S8(S[15]));
  ADD_8bits add_8bits_4 (
    .B9(RS1[0]), .B10(RS1[1]), .B11(RS1[2]), .B12(RS1[3]), .B13(RS1[4]), .B14(RS1[5]), .B15(RS1[6]),
    .B16(RS1[7]), .B1(RS2[0]), .B2(RS2[1]), .B3(RS2[2]), .B4(RS2[3]), .B5(RS2[4]), .B6(RS2[5]), .B7(RS2[6]),
    .B8(RS2[7]), .Cin(1'b0), .S6(S[5]), .S5(S[4]), .S4(S[3]), .S3(S[2]), .S2(S[1]), .S1(S[0]), .S7(S[6]),
    .Cout(add_8bits_4_cout), .S8(S[7]));
endmodule
