// Digital circuit ADD_2bits.dig as structural Verilog
module ADD_2bits (
  input  B1,
  input  B2,
  input  Cin,
  output S,
  output Cout
);

  wire and_1_out, and_2_out, and_3_out;

  xor xor_1 (S, Cin, B1, B2);
  and and_1 (and_1_out, B1, B2);
  and and_2 (and_2_out, Cin, B2);
  or or_1 (Cout, and_3_out, and_2_out, and_1_out);
  and and_3 (and_3_out, Cin, B1);
endmodule
