// Digital circuit ADD_8bits.dig as structural Verilog
module ADD_8bits (
  input  B9,
  input  B10,
  input  B11,
  input  B12,
  input  B13,
  input  B14,
  input  B15,
  input  B16,
  input  B1,
  input  B2,
  input  B3,
  input  B4,
  input  B5,
  input  B6,
  input  B7,
  input  B8,
  input  Cin,
  output S6,
  output S5,
  output S4,
  output S3,
  output S2,
  output S1,
  output S7,
  output Cout,
  output S8
);

  wire add_2bits_1_cout, add_2bits_2_cout, add_2bits_3_cout, add_2bits_4_cout, add_2bits_5_cout,
       add_2bits_6_cout, add_2bits_7_cout;

  ADD_2bits add_2bits_1 (.B1(B1), .B2(B9), .Cin(Cin), .S(S1), .Cout(add_2bits_1_cout));
  ADD_2bits add_2bits_2 (.B1(B2), .B2(B10), .Cin(add_2bits_1_cout), .S(S2), .Cout(add_2bits_2_cout));
  ADD_2bits add_2bits_3 (.B1(B3), .B2(B11), .Cin(add_2bits_2_cout), .S(S3), .Cout(add_2bits_3_cout));
  ADD_2bits add_2bits_4 (.B1(B4), .B2(B12), .Cin(add_2bits_3_cout), .S(S4), .Cout(add_2bits_4_cout));
  ADD_2bits add_2bits_5 (.B1(B5), .B2(B13), .Cin(add_2bits_4_cout), .S(S5), .Cout(add_2bits_5_cout));
  ADD_2bits add_2bits_6 (.B1(B6), .B2(B14), .Cin(add_2bits_5_cout), .S(S6), .Cout(add_2bits_6_cout));
  ADD_2bits add_2bits_7 (.B1(B7), .B2(B15), .Cin(add_2bits_6_cout), .S(S7), .Cout(add_2bits_7_cout));
  ADD_2bits add_2bits_8 (.B1(B8), .B2(B16), .Cin(add_2bits_7_cout), .S(S8), .Cout(Cout));
endmodule
