// Digital circuit AND.dig as structural Verilog
module AND (
  input  [31:0] RS1,
  input  [31:0] RS2,
  output [31:0] S
);

  and and_1 (S[0], RS1[0], RS2[0]);
  and and_2 (S[1], RS1[1], RS2[1]);
  and and_3 (S[2], RS1[2], RS2[2]);
  and and_4 (S[3], RS1[3], RS2[3]);
  and and_5 (S[4], RS1[4], RS2[4]);
  and and_6 (S[5], RS1[5], RS2[5]);
  and and_7 (S[6], RS1[6], RS2[6]);
  and and_8 (S[7], RS1[7], RS2[7]);
  and and_9 (S[8], RS1[8], RS2[8]);
  and and_10 (S[9], RS1[9], RS2[9]);
  and and_11 (S[10], RS1[10], RS2[10]);
  and and_12 (S[11], RS1[11], RS2[11]);
  and and_13 (S[12], RS1[12], RS2[12]);
  and and_14 (S[13], RS1[13], RS2[13]);
  and and_15 (S[14], RS1[14], RS2[14]);
  and and_16 (S[15], RS1[15], RS2[15]);
  and and_17 (S[16], RS1[16], RS2[16]);
  and and_18 (S[17], RS1[17], RS2[17]);
  and and_19 (S[18], RS1[18], RS2[18]);
  and and_20 (S[19], RS1[19], RS2[19]);
  and and_21 (S[20], RS1[20], RS2[20]);
  and and_22 (S[21], RS1[21], RS2[21]);
  and and_23 (S[22], RS1[22], RS2[22]);
  and and_24 (S[23], RS1[23], RS2[23]);
  and and_25 (S[24], RS1[24], RS2[24]);
  and and_26 (S[25], RS1[25], RS2[25]);
  and and_27 (S[26], RS1[26], RS2[26]);
  and and_28 (S[27], RS1[27], RS2[27]);
  and and_29 (S[28], RS1[28], RS2[28]);
  and and_30 (S[29], RS1[29], RS2[29]);
  and and_31 (S[30], RS1[30], RS2[30]);
  and and_32 (S[31], RS1[31], RS2[31]);
endmodule
