// Digital circuit BRG.dig as structural Verilog
module BRG (
  input  [4:0] RS1,
  input  [4:0] RS2,
  input  [4:0] RD,
  input  MWRITE,
  input  CLK,
  input  [31:0] DADO,
  output [31:0] S1,
  output [31:0] S2
);

  wire not_1_out;
  wire [7:0] demultiplexer_1_out_7, demultiplexer_1_out_15, demultiplexer_1_out_23, demultiplexer_1_out_31;
  wire [31:0] multiplexer_1_out, multiplexer_2_out, multiplexer_3_out, multiplexer_4_out, multiplexer_5_out,
       multiplexer_6_out, multiplexer_7_out, multiplexer_8_out, multiplexer_9_out, multiplexer_10_out,
       multiplexer_11_out, multiplexer_12_out, multiplexer_13_out, multiplexer_14_out, multiplexer_15_out,
       multiplexer_16_out, multiplexer_17_out, multiplexer_18_out, multiplexer_19_out, multiplexer_20_out,
       multiplexer_21_out, multiplexer_22_out, multiplexer_23_out, multiplexer_24_out, multiplexer_25_out,
       multiplexer_26_out, multiplexer_27_out, multiplexer_28_out, multiplexer_29_out, multiplexer_30_out,
       multiplexer_31_out, reg_1_s, reg_2_s, reg_3_s, reg_4_s, reg_5_s, reg_6_s, reg_7_s, reg_8_s, reg_9_s,
       reg_10_s, reg_11_s, reg_12_s, reg_13_s, reg_14_s, reg_15_s, reg_16_s, reg_17_s, reg_18_s, reg_19_s,
       reg_20_s, reg_21_s, reg_22_s, reg_23_s, reg_24_s, reg_25_s, reg_26_s, reg_27_s, reg_28_s, reg_29_s,
       reg_30_s, reg_31_s;

  not not_1 (not_1_out, CLK);
  Multiplexer #(.Bits(32)) multiplexer_1 (
    .sel(demultiplexer_1_out_31[0]), .in_0(reg_1_s), .in_1(DADO), .out(multiplexer_1_out));
  Multiplexer #(.Bits(32)) multiplexer_2 (
    .sel(demultiplexer_1_out_31[1]), .in_0(reg_2_s), .in_1(DADO), .out(multiplexer_2_out));
  Multiplexer #(.Bits(32)) multiplexer_3 (
    .sel(demultiplexer_1_out_31[2]), .in_0(reg_3_s), .in_1(DADO), .out(multiplexer_3_out));
  Multiplexer #(.Bits(32)) multiplexer_4 (
    .sel(demultiplexer_1_out_31[3]), .in_0(reg_4_s), .in_1(DADO), .out(multiplexer_4_out));
  Multiplexer #(.Bits(32)) multiplexer_5 (
    .sel(demultiplexer_1_out_31[4]), .in_0(reg_5_s), .in_1(DADO), .out(multiplexer_5_out));
  Multiplexer #(.Bits(32)) multiplexer_6 (
    .sel(demultiplexer_1_out_31[5]), .in_0(reg_6_s), .in_1(DADO), .out(multiplexer_6_out));
  Multiplexer #(.Bits(32)) multiplexer_7 (
    .sel(demultiplexer_1_out_31[6]), .in_0(reg_7_s), .in_1(DADO), .out(multiplexer_7_out));
  Multiplexer #(.Bits(32)) multiplexer_8 (
    .sel(demultiplexer_1_out_31[7]), .in_0(reg_8_s), .in_1(DADO), .out(multiplexer_8_out));
  REG reg_1 (.CLK(not_1_out), .E(multiplexer_1_out), .S(reg_1_s));
  REG reg_2 (.CLK(not_1_out), .E(multiplexer_2_out), .S(reg_2_s));
  REG reg_3 (.CLK(not_1_out), .E(multiplexer_3_out), .S(reg_3_s));
  REG reg_4 (.CLK(not_1_out), .E(multiplexer_4_out), .S(reg_4_s));
  REG reg_5 (.CLK(not_1_out), .E(multiplexer_5_out), .S(reg_5_s));
  REG reg_6 (.CLK(not_1_out), .E(multiplexer_6_out), .S(reg_6_s));
  REG reg_7 (.CLK(not_1_out), .E(multiplexer_7_out), .S(reg_7_s));
  REG reg_8 (.CLK(not_1_out), .E(multiplexer_8_out), .S(reg_8_s));
  Multiplexer #(.Bits(32)) multiplexer_9 (
    .sel(demultiplexer_1_out_23[0]), .in_0(reg_9_s), .in_1(DADO), .out(multiplexer_9_out));
  Multiplexer #(.Bits(32)) multiplexer_10 (
    .sel(demultiplexer_1_out_23[1]), .in_0(reg_10_s), .in_1(DADO), .out(multiplexer_10_out));
  Multiplexer #(.Bits(32)) multiplexer_11 (
    .sel(demultiplexer_1_out_23[2]), .in_0(reg_11_s), .in_1(DADO), .out(multiplexer_11_out));
  Multiplexer #(.Bits(32)) multiplexer_12 (
    .sel(demultiplexer_1_out_23[3]), .in_0(reg_12_s), .in_1(DADO), .out(multiplexer_12_out));
  Multiplexer #(.Bits(32)) multiplexer_13 (
    .sel(demultiplexer_1_out_23[4]), .in_0(reg_13_s), .in_1(DADO), .out(multiplexer_13_out));
  Multiplexer #(.Bits(32)) multiplexer_14 (
    .sel(demultiplexer_1_out_23[5]), .in_0(reg_14_s), .in_1(DADO), .out(multiplexer_14_out));
  Multiplexer #(.Bits(32)) multiplexer_15 (
    .sel(demultiplexer_1_out_23[6]), .in_0(reg_15_s), .in_1(DADO), .out(multiplexer_15_out));
  Multiplexer #(.Bits(32)) multiplexer_16 (
    .sel(demultiplexer_1_out_23[7]), .in_0(reg_16_s), .in_1(DADO), .out(multiplexer_16_out));
  REG reg_9 (.CLK(not_1_out), .E(multiplexer_9_out), .S(reg_9_s));
  REG reg_10 (.CLK(not_1_out), .E(multiplexer_10_out), .S(reg_10_s));
  REG reg_11 (.CLK(not_1_out), .E(multiplexer_11_out), .S(reg_11_s));
  REG reg_12 (.CLK(not_1_out), .E(multiplexer_12_out), .S(reg_12_s));
  REG reg_13 (.CLK(not_1_out), .E(multiplexer_13_out), .S(reg_13_s));
  REG reg_14 (.CLK(not_1_out), .E(multiplexer_14_out), .S(reg_14_s));
  REG reg_15 (.CLK(not_1_out), .E(multiplexer_15_out), .S(reg_15_s));
  REG reg_16 (.CLK(not_1_out), .E(multiplexer_16_out), .S(reg_16_s));
  Multiplexer #(.Bits(32)) multiplexer_17 (
    .sel(demultiplexer_1_out_15[0]), .in_0(reg_17_s), .in_1(DADO), .out(multiplexer_17_out));
  Multiplexer #(.Bits(32)) multiplexer_18 (
    .sel(demultiplexer_1_out_15[1]), .in_0(reg_18_s), .in_1(DADO), .out(multiplexer_18_out));
  Multiplexer #(.Bits(32)) multiplexer_19 (
    .sel(demultiplexer_1_out_15[2]), .in_0(reg_19_s), .in_1(DADO), .out(multiplexer_19_out));
  Multiplexer #(.Bits(32)) multiplexer_20 (
    .sel(demultiplexer_1_out_15[3]), .in_0(reg_20_s), .in_1(DADO), .out(multiplexer_20_out));
  Multiplexer #(.Bits(32)) multiplexer_21 (
    .sel(demultiplexer_1_out_15[4]), .in_0(reg_21_s), .in_1(DADO), .out(multiplexer_21_out));
  Multiplexer #(.Bits(32)) multiplexer_22 (
    .sel(demultiplexer_1_out_15[5]), .in_0(reg_22_s), .in_1(DADO), .out(multiplexer_22_out));
  Multiplexer #(.Bits(32)) multiplexer_23 (
    .sel(demultiplexer_1_out_15[6]), .in_0(reg_23_s), .in_1(DADO), .out(multiplexer_23_out));
  Multiplexer #(.Bits(32)) multiplexer_24 (
    .sel(demultiplexer_1_out_15[7]), .in_0(reg_24_s), .in_1(DADO), .out(multiplexer_24_out));
  REG reg_17 (.CLK(not_1_out), .E(multiplexer_17_out), .S(reg_17_s));
  REG reg_18 (.CLK(not_1_out), .E(multiplexer_18_out), .S(reg_18_s));
  REG reg_19 (.CLK(not_1_out), .E(multiplexer_19_out), .S(reg_19_s));
  REG reg_20 (.CLK(not_1_out), .E(multiplexer_20_out), .S(reg_20_s));
  REG reg_21 (.CLK(not_1_out), .E(multiplexer_21_out), .S(reg_21_s));
  REG reg_22 (.CLK(not_1_out), .E(multiplexer_22_out), .S(reg_22_s));
  REG reg_23 (.CLK(not_1_out), .E(multiplexer_23_out), .S(reg_23_s));
  REG reg_24 (.CLK(not_1_out), .E(multiplexer_24_out), .S(reg_24_s));
  Demultiplexer #(.Selector_Bits(5)) demultiplexer_1 (
    .sel(RD), .in(MWRITE), .out_0(demultiplexer_1_out_7[0]), .out_1(demultiplexer_1_out_7[1]),
    .out_2(demultiplexer_1_out_7[2]), .out_3(demultiplexer_1_out_7[3]), .out_4(demultiplexer_1_out_7[4]),
    .out_5(demultiplexer_1_out_7[5]), .out_6(demultiplexer_1_out_7[6]), .out_7(demultiplexer_1_out_7[7]),
    .out_8(demultiplexer_1_out_15[0]), .out_9(demultiplexer_1_out_15[1]), .out_10(demultiplexer_1_out_15[2]),
    .out_11(demultiplexer_1_out_15[3]), .out_12(demultiplexer_1_out_15[4]),
    .out_13(demultiplexer_1_out_15[5]), .out_14(demultiplexer_1_out_15[6]),
    .out_15(demultiplexer_1_out_15[7]), .out_16(demultiplexer_1_out_23[0]),
    .out_17(demultiplexer_1_out_23[1]), .out_18(demultiplexer_1_out_23[2]),
    .out_19(demultiplexer_1_out_23[3]), .out_20(demultiplexer_1_out_23[4]),
    .out_21(demultiplexer_1_out_23[5]), .out_22(demultiplexer_1_out_23[6]),
    .out_23(demultiplexer_1_out_23[7]), .out_24(demultiplexer_1_out_31[0]),
    .out_25(demultiplexer_1_out_31[1]), .out_26(demultiplexer_1_out_31[2]),
    .out_27(demultiplexer_1_out_31[3]), .out_28(demultiplexer_1_out_31[4]),
    .out_29(demultiplexer_1_out_31[5]), .out_30(demultiplexer_1_out_31[6]), .out_31(demultiplexer_1_out_31[7]));
  REG reg_25 (.CLK(not_1_out), .E(multiplexer_25_out), .S(reg_25_s));
  Multiplexer #(.Bits(32)) multiplexer_25 (
    .sel(demultiplexer_1_out_7[1]), .in_0(reg_25_s), .in_1(DADO), .out(multiplexer_25_out));
  REG reg_26 (.CLK(not_1_out), .E(multiplexer_26_out), .S(reg_26_s));
  Multiplexer #(.Bits(32)) multiplexer_26 (
    .sel(demultiplexer_1_out_7[2]), .in_0(reg_26_s), .in_1(DADO), .out(multiplexer_26_out));
  REG reg_27 (.CLK(not_1_out), .E(multiplexer_27_out), .S(reg_27_s));
  Multiplexer #(.Bits(32)) multiplexer_27 (
    .sel(demultiplexer_1_out_7[3]), .in_0(reg_27_s), .in_1(DADO), .out(multiplexer_27_out));
  REG reg_28 (.CLK(not_1_out), .E(multiplexer_28_out), .S(reg_28_s));
  Multiplexer #(.Bits(32)) multiplexer_28 (
    .sel(demultiplexer_1_out_7[4]), .in_0(reg_28_s), .in_1(DADO), .out(multiplexer_28_out));
  REG reg_29 (.CLK(not_1_out), .E(multiplexer_29_out), .S(reg_29_s));
  Multiplexer #(.Bits(32)) multiplexer_29 (
    .sel(demultiplexer_1_out_7[5]), .in_0(reg_29_s), .in_1(DADO), .out(multiplexer_29_out));
  REG reg_30 (.CLK(not_1_out), .E(multiplexer_30_out), .S(reg_30_s));
  Multiplexer #(.Bits(32)) multiplexer_30 (
    .sel(demultiplexer_1_out_7[6]), .in_0(reg_30_s), .in_1(DADO), .out(multiplexer_30_out));
  REG reg_31 (.CLK(not_1_out), .E(multiplexer_31_out), .S(reg_31_s));
  Multiplexer #(.Bits(32)) multiplexer_31 (
    .sel(demultiplexer_1_out_7[7]), .in_0(reg_31_s), .in_1(DADO), .out(multiplexer_31_out));
  Multiplexer #(.Selector_Bits(5), .Bits(32)) multiplexer_32 (
    .sel(RS1), .in_0({32{1'b0}}), .in_1(reg_25_s), .in_2(reg_26_s), .in_3(reg_27_s), .in_4(reg_28_s),
    .in_5(reg_29_s), .in_6(reg_30_s), .in_7(reg_31_s), .in_8(reg_17_s), .in_9(reg_18_s), .in_10(reg_19_s),
    .in_11(reg_20_s), .in_12(reg_21_s), .in_13(reg_22_s), .in_14(reg_23_s), .in_15(reg_24_s),
    .in_16(reg_9_s), .in_17(reg_10_s), .in_18(reg_11_s), .in_19(reg_12_s), .in_20(reg_13_s),
    .in_21(reg_14_s), .in_22(reg_15_s), .in_23(reg_16_s), .in_24(reg_1_s), .in_25(reg_2_s), .in_26(reg_3_s),
    .in_27(reg_4_s), .in_28(reg_5_s), .in_29(reg_6_s), .in_30(reg_7_s), .in_31(reg_8_s), .out(S1));
  Multiplexer #(.Selector_Bits(5), .Bits(32)) multiplexer_33 (
    .sel(RS2), .in_0({32{1'b0}}), .in_1(reg_25_s), .in_2(reg_26_s), .in_3(reg_27_s), .in_4(reg_28_s),
    .in_5(reg_29_s), .in_6(reg_30_s), .in_7(reg_31_s), .in_8(reg_17_s), .in_9(reg_18_s), .in_10(reg_19_s),
    .in_11(reg_20_s), .in_12(reg_21_s), .in_13(reg_22_s), .in_14(reg_23_s), .in_15(reg_24_s),
    .in_16(reg_9_s), .in_17(reg_10_s), .in_18(reg_11_s), .in_19(reg_12_s), .in_20(reg_13_s),
    .in_21(reg_14_s), .in_22(reg_15_s), .in_23(reg_16_s), .in_24(reg_1_s), .in_25(reg_2_s), .in_26(reg_3_s),
    .in_27(reg_4_s), .in_28(reg_5_s), .in_29(reg_6_s), .in_30(reg_7_s), .in_31(reg_8_s), .out(S2));
endmodule
