// Digital circuit CC.dig as structural Verilog
module CC (
  input  [6:0] OPCD,
  input  [2:0] F3,
  input  [6:0] F7,
  input  [31:0] SULA,
  output IMM,
  output BRG,
  output STR,
  output LD,
  output [1:0] PC,
  output [1:0] DADO,
  output [1:0] TPIMM,
  output [2:0] ULA
);

  wire _0x0, _0x00, _0x1, _0x2, _0x4, _0x5, _0x6, _0x7, _0x20, _0000011, _0010011, _0100011, _0110011,
       _1100011, _1100111, and_1_out, and_2_out, and_3_out, and_4_out, and_5_out, and_6_out, and_7_out,
       and_10_out, and_14_out, and_16_out, and_18_out, and_21_out, and_23_out, and_25_out, and_27_out,
       and_28_out, and_29_out, and_31_out, and_32_out, and_33_out, and_35_out, and_36_out, and_37_out,
       and_39_out, and_40_out, and_41_out, and_43_out, and_44_out, and_45_out, and_46_out, and_47_out,
       and_48_out, and_49_out, not_1_out, not_2_out, not_3_out, not_4_out, not_5_out, not_6_out, not_9_out,
       not_10_out, not_11_out, not_12_out, not_13_out, not_14_out, not_15_out, not_16_out, not_17_out,
       not_18_out, not_19_out, not_20_out, not_21_out, not_22_out, not_25_out, not_26_out, not_27_out,
       not_28_out, not_29_out, not_30_out, not_31_out, not_32_out, not_34_out, not_35_out, not_36_out,
       not_37_out, not_40_out, not_41_out, not_43_out, not_44_out, not_45_out, not_47_out, not_48_out,
       or_2_out, or_4_out, or_5_out, or_6_out, or_7_out, or_8_out, or_9_out, or_10_out, or_11_out, or_12_out;
  wire [1:0] not_38_out;
  wire [1:1] not_42_out, rom_1_d;
  wire [2:0] and_50_out, and_52_out, and_54_out, multiplexer_1_out, multiplexer_2_out, multiplexer_3_out,
       multiplexer_4_out, multiplexer_5_out, multiplexer_6_out, multiplexer_7_out, multiplexer_8_out,
       multiplexer_9_out, multiplexer_10_out, multiplexer_11_out, multiplexer_12_out, multiplexer_13_out,
       multiplexer_14_out, multiplexer_15_out, not_23_out, not_46_out, not_49_out, or_3_out, or_13_out;
  wire [2:1] and_51_out, and_53_out, not_7_out;
  wire [2:2] not_33_out, or_14_out;

  and and_1 (and_1_out, _0x0, SULA[0]);
  or or_1 (PC[1], and_2_out, and_5_out);
  and and_2 (and_2_out, or_2_out, _1100011);
  or or_2 (or_2_out, and_1_out, and_3_out, and_4_out, and_6_out);
  and and_3 (and_3_out, _0x1, not_1_out);
  not not_1 (not_1_out, SULA[0]);
  and and_4 (and_4_out, _0x4, SULA[0]);
  not not_2 (not_2_out, _1100011);
  and and_5 (and_5_out, rom_1_d[1], not_2_out);
  and and_6 (and_6_out, _0x5, not_3_out);
  not not_3 (not_3_out, SULA[0]);
  ROM #(.AddrBits(3), .Bits(10)) rom_1 (
    .A(or_3_out), .sel(1'b1), .D({IMM, TPIMM, BRG, STR, LD, rom_1_d[1], PC[0], DADO}));
  assign or_3_out = multiplexer_7_out | multiplexer_6_out | multiplexer_5_out | multiplexer_4_out | multiplexer_3_out | multiplexer_2_out | multiplexer_1_out;  // Or or_3, 3 bits wide
  not not_4 (not_4_out, OPCD[6]);
  Multiplexer #(.Bits(3)) multiplexer_1 (
    .sel(_0110011), .in_0(3'b000), .in_1({not_7_out, _0110011}), .out(multiplexer_1_out));
  not not_5 (not_5_out, F3[0]);
  not not_6 (not_6_out, F3[1]);
  and and_7 (and_7_out, OPCD[5], not_4_out);
  not not_7 (not_7_out[1], _0110011);
  not not_8 (not_7_out[2], _0110011);
  not not_9 (not_9_out, F3[2]);
  not not_10 (not_10_out, F3[1]);
  and and_8 (_0x0, not_9_out, not_6_out, not_5_out);
  not not_11 (not_11_out, F7[0]);
  not not_12 (not_12_out, F7[1]);
  and and_9 (_0x00, not_12_out, not_11_out);
  not not_13 (not_13_out, OPCD[3]);
  not not_14 (not_14_out, OPCD[2]);
  and and_10 (and_10_out, not_13_out, OPCD[4]);
  and and_11 (_0110011, and_14_out, and_10_out, and_7_out);
  not not_15 (not_15_out, F3[2]);
  not not_16 (not_16_out, F3[0]);
  and and_12 (_0x1, not_15_out, not_10_out, F3[0]);
  not not_17 (not_17_out, F7[0]);
  and and_13 (_0x20, F7[1], not_17_out);
  not not_18 (not_18_out, OPCD[6]);
  and and_14 (and_14_out, OPCD[0], OPCD[1], not_14_out);
  Multiplexer #(.Bits(3)) multiplexer_2 (
    .sel(_0010011), .in_0(3'b000), .in_1({not_23_out[2], _0010011, not_23_out[0]}), .out(multiplexer_2_out));
  not not_19 (not_19_out, F3[2]);
  not not_20 (not_20_out, F3[1]);
  not not_21 (not_21_out, F3[0]);
  and and_15 (_0x2, not_19_out, F3[1], not_16_out);
  not not_22 (not_22_out, OPCD[5]);
  and and_16 (and_16_out, not_22_out, not_18_out);
  not not_23 (not_23_out[0], _0010011);
  not not_24 (not_23_out[2], _0010011);
  not not_25 (not_25_out, F3[1]);
  and and_17 (_0x4, F3[2], not_20_out, not_21_out);
  not not_26 (not_26_out, OPCD[3]);
  not not_27 (not_27_out, OPCD[2]);
  and and_18 (and_18_out, not_26_out, OPCD[4]);
  and and_19 (_0010011, and_21_out, and_18_out, and_16_out);
  not not_28 (not_28_out, F3[0]);
  and and_20 (_0x5, F3[2], not_25_out, F3[0]);
  and and_21 (and_21_out, OPCD[0], OPCD[1], not_27_out);
  and and_22 (_0x6, F3[2], F3[1], not_28_out);
  not not_29 (not_29_out, OPCD[6]);
  not not_30 (not_30_out, OPCD[5]);
  and and_23 (and_23_out, not_30_out, not_29_out);
  Multiplexer #(.Bits(3)) multiplexer_3 (
    .sel(_0000011), .in_0(3'b000), .in_1({not_33_out[2], {2{_0000011}}}), .out(multiplexer_3_out));
  and and_24 (_0x7, F3[2], F3[1], F3[0]);
  not not_31 (not_31_out, OPCD[4]);
  not not_32 (not_32_out, OPCD[3]);
  and and_25 (and_25_out, not_32_out, not_31_out);
  and and_26 (_0000011, and_27_out, and_25_out, and_23_out);
  not not_33 (not_33_out[2], _0000011);
  not not_34 (not_34_out, OPCD[2]);
  and and_27 (and_27_out, OPCD[0], OPCD[1], not_34_out);
  not not_35 (not_35_out, OPCD[6]);
  and and_28 (and_28_out, OPCD[5], not_35_out);
  Multiplexer #(.Bits(3)) multiplexer_4 (
    .sel(_0100011), .in_0(3'b000), .in_1({_0100011, not_38_out}), .out(multiplexer_4_out));
  not not_36 (not_36_out, OPCD[4]);
  not not_37 (not_37_out, OPCD[3]);
  and and_29 (and_29_out, not_37_out, not_36_out);
  and and_30 (_0100011, and_31_out, and_29_out, and_28_out);
  not not_38 (not_38_out[0], _0100011);
  not not_39 (not_38_out[1], _0100011);
  not not_40 (not_40_out, OPCD[2]);
  and and_31 (and_31_out, OPCD[0], OPCD[1], not_40_out);
  Multiplexer #(.Bits(3)) multiplexer_5 (
    .sel(_1100011), .in_0(3'b000), .in_1({_1100011, not_42_out[1], _1100011}), .out(multiplexer_5_out));
  not not_41 (not_41_out, OPCD[4]);
  and and_32 (and_32_out, OPCD[5], OPCD[6]);
  not not_42 (not_42_out[1], _1100011);
  not not_43 (not_43_out, OPCD[3]);
  not not_44 (not_44_out, OPCD[2]);
  and and_33 (and_33_out, not_43_out, not_41_out);
  and and_34 (_1100011, and_35_out, and_33_out, and_32_out);
  and and_35 (and_35_out, OPCD[0], OPCD[1], not_44_out);
  Multiplexer #(.Bits(3)) multiplexer_6 (
    .sel(not_46_out[2]), .in_0(3'b000), .in_1({{2{not_46_out[2]}}, not_46_out[0]}), .out(multiplexer_6_out));
  not not_45 (not_45_out, OPCD[4]);
  and and_36 (and_36_out, OPCD[5], OPCD[6]);
  not not_46 (not_46_out[0], not_46_out[2]);
  and and_37 (and_37_out, OPCD[3], not_45_out);
  and and_38 (not_46_out[2], and_39_out, and_37_out, and_36_out);
  and and_39 (and_39_out, OPCD[0], OPCD[1], OPCD[2]);
  and and_40 (and_40_out, OPCD[5], OPCD[6]);
  Multiplexer #(.Bits(3)) multiplexer_7 (.sel(_1100111), .in_0(3'b000), .in_1({3{_1100111}}), .out(multiplexer_7_out));
  not not_47 (not_47_out, OPCD[4]);
  not not_48 (not_48_out, OPCD[3]);
  and and_41 (and_41_out, not_48_out, not_47_out);
  and and_42 (_1100111, and_43_out, and_41_out, and_40_out);
  and and_43 (and_43_out, OPCD[0], OPCD[1], OPCD[2]);
  and and_44 (and_44_out, _0x00, _0110011);
  or or_4 (or_4_out, and_44_out, _1100111, _0010011);
  or or_5 (or_5_out, _0000011, _0100011);
  or or_6 (or_6_out, _0110011, _0010011);
  or or_7 (or_7_out, _0x4, _0x5);
  or or_8 (or_8_out, _0x1, _0x0);
  and and_45 (and_45_out, or_4_out, _0x0);
  and and_46 (and_46_out, or_5_out, _0x2);
  or or_9 (or_9_out, _0110011, _0010011);
  or or_10 (or_10_out, _0110011, _0010011);
  or or_11 (or_11_out, _0110011, _0010011);
  or or_12 (or_12_out, _0110011, _0010011);
  and and_47 (and_47_out, or_6_out, _0x2);
  and and_48 (and_48_out, _1100011, or_7_out);
  and and_49 (and_49_out, or_8_out, _1100011);
  or or_13 (or_13_out[0], and_45_out, and_46_out);
  and and_50 (and_50_out[1], _0110011, _0x20, _0x0);
  and and_51 (and_51_out[1], or_9_out, _0x4);
  and and_52 (and_52_out[2], or_10_out, _0x6);
  and and_53 (and_53_out[2], or_11_out, _0x7);
  and and_54 (and_54_out[2], or_12_out, _0x1);
  or or_14 (or_14_out[2], and_47_out, and_48_out);
  not not_49 (not_49_out[0], and_49_out);
  not not_50 (not_49_out[1], and_49_out);
  not not_51 (not_49_out[2], and_49_out);
  not not_52 (or_13_out[1], or_13_out[0]);
  not not_53 (or_13_out[2], or_13_out[0]);
  not not_54 (and_50_out[0], and_50_out[1]);
  not not_55 (and_50_out[2], and_50_out[1]);
  not not_56 (and_51_out[2], and_51_out[1]);
  not not_57 (and_52_out[0], and_52_out[2]);
  not not_58 (and_52_out[1], and_52_out[2]);
  not not_59 (and_53_out[1], and_53_out[2]);
  not not_60 (and_54_out[0], and_54_out[2]);
  Multiplexer #(.Bits(3)) multiplexer_8 (.sel(and_49_out), .in_0(3'b000), .in_1(not_49_out), .out(multiplexer_8_out));
  Multiplexer #(.Bits(3)) multiplexer_9 (.sel(or_13_out[0]), .in_0(3'b000), .in_1(or_13_out), .out(multiplexer_9_out));
  Multiplexer #(.Bits(3)) multiplexer_10 (
    .sel(and_50_out[1]), .in_0(3'b000), .in_1(and_50_out), .out(multiplexer_10_out));
  Multiplexer #(.Bits(3)) multiplexer_11 (
    .sel(and_51_out[1]), .in_0(3'b000), .in_1({and_51_out, and_51_out[1]}), .out(multiplexer_11_out));
  Multiplexer #(.Bits(3)) multiplexer_12 (
    .sel(and_52_out[2]), .in_0(3'b000), .in_1(and_52_out), .out(multiplexer_12_out));
  Multiplexer #(.Bits(3)) multiplexer_13 (
    .sel(and_53_out[2]), .in_0(3'b000), .in_1({and_53_out, and_53_out[2]}), .out(multiplexer_13_out));
  Multiplexer #(.Bits(3)) multiplexer_14 (
    .sel(and_54_out[2]), .in_0(3'b000), .in_1({{2{and_54_out[2]}}, and_54_out[0]}), .out(multiplexer_14_out));
  Multiplexer #(.Bits(3)) multiplexer_15 (
    .sel(or_14_out[2]), .in_0(3'b000), .in_1({3{or_14_out[2]}}), .out(multiplexer_15_out));
  assign ULA = multiplexer_8_out | multiplexer_9_out | multiplexer_10_out | multiplexer_11_out | multiplexer_12_out | multiplexer_13_out | multiplexer_14_out | multiplexer_15_out;  // Or or_15, 3 bits wide

  // Notes on the sheet:
  //   contents of rom_1 (hex, n*v repeats v):
  //   0,47,3c7,3d6,324,8c,4d,3c9
endmodule
