// Digital circuit IMMEXT.dig as structural Verilog
module IMMEXT (
  input  [24:0] E,
  input  [1:0] TPIMM,
  output [31:0] S
);

  wire [6:6] undriven, undriven_2;

  Multiplexer #(.Selector_Bits(2)) multiplexer_1 (
    .sel(TPIMM), .in_2(E[0]), .in_3(E[13]), .out(S[0]));  // open: in_0, in_1
  // Pins of 20 and 25 bits meet at E
  // Pins of 6 and 7 bits meet at {undriven[6], E[23:18]}
  // Pins of 1 and 32 bits meet at {{20{E[24]}}, undriven[6], E[23:13]}
  // Pins of 1 and 32 bits meet at S
  // Pins of 1 and 32 bits meet at {{20{E[24]}}, undriven_2[6], E[23:18], E[4:0]}
  // Pins of 6 and 7 bits meet at {undriven_2[6], E[23:18]}
endmodule
