// Digital circuit OR.dig as structural Verilog
module OR (
  input  [31:0] RS1,
  input  [31:0] RS2,
  output [31:0] S
);

  or or_1 (S[0], RS1[0], RS2[0]);
  or or_2 (S[1], RS1[1], RS2[1]);
  or or_3 (S[2], RS1[2], RS2[2]);
  or or_4 (S[3], RS1[3], RS2[3]);
  or or_5 (S[4], RS1[4], RS2[4]);
  or or_6 (S[5], RS1[5], RS2[5]);
  or or_7 (S[6], RS1[6], RS2[6]);
  or or_8 (S[7], RS1[7], RS2[7]);
  or or_9 (S[8], RS1[8], RS2[8]);
  or or_10 (S[9], RS1[9], RS2[9]);
  or or_11 (S[10], RS1[10], RS2[10]);
  or or_12 (S[11], RS1[11], RS2[11]);
  or or_13 (S[12], RS1[12], RS2[12]);
  or or_14 (S[13], RS1[13], RS2[13]);
  or or_15 (S[14], RS1[14], RS2[14]);
  or or_16 (S[15], RS1[15], RS2[15]);
  or or_17 (S[16], RS1[16], RS2[16]);
  or or_18 (S[17], RS1[17], RS2[17]);
  or or_19 (S[18], RS1[18], RS2[18]);
  or or_20 (S[19], RS1[19], RS2[19]);
  or or_21 (S[20], RS1[20], RS2[20]);
  or or_22 (S[21], RS1[21], RS2[21]);
  or or_23 (S[22], RS1[22], RS2[22]);
  or or_24 (S[23], RS1[23], RS2[23]);
  or or_25 (S[24], RS1[24], RS2[24]);
  or or_26 (S[25], RS1[25], RS2[25]);
  or or_27 (S[26], RS1[26], RS2[26]);
  or or_28 (S[27], RS1[27], RS2[27]);
  or or_29 (S[28], RS1[28], RS2[28]);
  or or_30 (S[29], RS1[29], RS2[29]);
  or or_31 (S[30], RS1[30], RS2[30]);
  or or_32 (S[31], RS1[31], RS2[31]);
endmodule
