// Digital circuit OR_32.dig as structural Verilog
module OR_32 (
  input  [31:0] E,
  output [31:0] S
);

  wire or_1_out, or_2_out, or_3_out, or_4_out, or_5_out, or_7_out, or_8_out, or_9_out, or_10_out, or_11_out;

  or or_1 (or_1_out, E[28], E[29], E[30], E[31]);
  or or_2 (or_2_out, E[24], E[25], E[26], E[27]);
  or or_3 (or_3_out, E[20], E[21], E[22], E[23]);
  or or_4 (or_4_out, or_5_out, or_3_out, or_2_out, or_1_out);
  or or_5 (or_5_out, E[16], E[17], E[18], E[19]);
  or or_6 (S[31], or_10_out, or_4_out);
  or or_7 (or_7_out, E[12], E[13], E[14], E[15]);
  or or_8 (or_8_out, E[8], E[9], E[10], E[11]);
  or or_9 (or_9_out, E[4], E[5], E[6], E[7]);
  or or_10 (or_10_out, or_11_out, or_9_out, or_8_out, or_7_out);
  or or_11 (or_11_out, E[0], E[1], E[2], E[3]);

  assign S[30:0] = {31{S[31]}};
endmodule
