// Digital circuit ProjetoMicroarquitetural.dig as structural Verilog
module ProjetoMicroarquitetural (
  input  clk
);

  wire IMM, LD, MWRITE, STR;
  wire [1:0] DADO, PC, TPIMM;
  wire [2:0] F3, ULA;
  wire [4:0] RD, RS1, RS2;
  wire [6:0] F7, OPCODE;
  wire [31:0] add_1_s, add_2_s, add_3_s, brg_1_s1, MDD_d, multiplexer_1_out, multiplexer_2_out, SDADO, SIMM,
       SPC, SRS2, SULA;

  REG u_PC (.CLK(clk), .E(multiplexer_1_out), .S(SPC));
  Multiplexer #(.Selector_Bits(2), .Bits(32)) multiplexer_1 (
    .sel(PC), .in_0(SPC), .in_1(add_2_s), .in_2(SULA), .in_3(add_1_s), .out(multiplexer_1_out));
  ROM #(.AddrBits(7), .isProgramMemory("true"), .Bits(32)) MI (
    .A(SPC[6:0]), .sel(1'b1), .D({F7, RS2, RS1, F3, RD, OPCODE}));
  // Probe on SPC
  ADD add_1 (.RS1(SPC), .RS2(SIMM), .S(add_1_s));  // open: Cout
  ADD add_2 (.RS1(SPC), .RS2(32'h4), .S(add_2_s));  // open: Cout
  CC cc_1 (
    .OPCD(OPCODE), .F3(F3), .F7(F7), .DADO(DADO), .PC(PC), .LD(LD), .STR(STR), .BRG(MWRITE), .TPIMM(TPIMM),
    .IMM(IMM), .SULA(SULA), .ULA(ULA));
  BRG brg_1 (.RS1(RS1), .RS2(RS2), .RD(RD), .MWRITE(MWRITE), .CLK(clk), .DADO(SDADO), .S1(brg_1_s1), .S2(SRS2));
  IMMEXT immext_1 (.E({F7, RS2, RS1, F3, RD}), .TPIMM(TPIMM), .S(SIMM));
  Multiplexer #(.Bits(32)) multiplexer_2 (.sel(IMM), .in_0(SRS2), .in_1(SIMM), .out(multiplexer_2_out));
  ULA ula_1 (.RS1(brg_1_s1), .RS2(multiplexer_2_out), .E(ULA), .S(SULA));  // open: ERRO
  RAMDualPort #(.AddrBits(5), .Bits(32)) MDD (.A(SULA[4:0]), .Din(SRS2), .str(STR), .C(clk), .ld(LD), .D(MDD_d));
  Multiplexer #(.Selector_Bits(2), .Bits(32)) multiplexer_3 (
    .sel(DADO), .in_0({32{1'b0}}), .in_1(add_3_s), .in_2(MDD_d), .in_3(SULA), .out(SDADO));
  ADD add_3 (.RS1(32'h4), .RS2(SPC), .S(add_3_s));  // open: Cout

  // Notes on the sheet:
  //   clk: Hz: 5
  //   contents of MI (hex, n*v repeats v):
  //   ff810113,0,0,0,100293,0,0,0,100313,0,0,0,513,0,0,0,1400e13,0,0,0
  //   ,200f93,0,0,0,512023,0,0,0,612223,0,0,0,10000ef,0,0,0,4f9f93,0,0,0
  //   ,1f10133,7*0,3cfd063,0,0,0,1f8f93,0,0,0,628533,0,0,0,ffc10113
  //   ,0,0,0,a12023,0,0,0,30293,0,0,0,50313,0,0,0,fe5ff06f,0,0,0,8067
endmodule
