// Digital circuit REG.dig as structural Verilog
module REG (
  input  CLK,
  input  [31:0] E,
  output [31:0] S
);

  D_FF d_ff_1 (.D(E[24]), .C(CLK), .Q(S[24]));  // open: nQ
  D_FF d_ff_2 (.D(E[25]), .C(CLK), .Q(S[25]));  // open: nQ
  D_FF d_ff_3 (.D(E[26]), .C(CLK), .Q(S[26]));  // open: nQ
  D_FF d_ff_4 (.D(E[27]), .C(CLK), .Q(S[27]));  // open: nQ
  D_FF d_ff_5 (.D(E[28]), .C(CLK), .Q(S[28]));  // open: nQ
  D_FF d_ff_6 (.D(E[29]), .C(CLK), .Q(S[29]));  // open: nQ
  D_FF d_ff_7 (.D(E[30]), .C(CLK), .Q(S[30]));  // open: nQ
  D_FF d_ff_8 (.D(E[31]), .C(CLK), .Q(S[31]));  // open: nQ
  D_FF d_ff_9 (.D(E[16]), .C(CLK), .Q(S[16]));  // open: nQ
  D_FF d_ff_10 (.D(E[17]), .C(CLK), .Q(S[17]));  // open: nQ
  D_FF d_ff_11 (.D(E[18]), .C(CLK), .Q(S[18]));  // open: nQ
  D_FF d_ff_12 (.D(E[19]), .C(CLK), .Q(S[19]));  // open: nQ
  D_FF d_ff_13 (.D(E[20]), .C(CLK), .Q(S[20]));  // open: nQ
  D_FF d_ff_14 (.D(E[21]), .C(CLK), .Q(S[21]));  // open: nQ
  D_FF d_ff_15 (.D(E[22]), .C(CLK), .Q(S[22]));  // open: nQ
  D_FF d_ff_16 (.D(E[23]), .C(CLK), .Q(S[23]));  // open: nQ
  D_FF d_ff_17 (.D(E[8]), .C(CLK), .Q(S[8]));  // open: nQ
  D_FF d_ff_18 (.D(E[9]), .C(CLK), .Q(S[9]));  // open: nQ
  D_FF d_ff_19 (.D(E[10]), .C(CLK), .Q(S[10]));  // open: nQ
  D_FF d_ff_20 (.D(E[11]), .C(CLK), .Q(S[11]));  // open: nQ
  D_FF d_ff_21 (.D(E[12]), .C(CLK), .Q(S[12]));  // open: nQ
  D_FF d_ff_22 (.D(E[13]), .C(CLK), .Q(S[13]));  // open: nQ
  D_FF d_ff_23 (.D(E[14]), .C(CLK), .Q(S[14]));  // open: nQ
  D_FF d_ff_24 (.D(E[15]), .C(CLK), .Q(S[15]));  // open: nQ
  D_FF d_ff_25 (.D(E[0]), .C(CLK), .Q(S[0]));  // open: nQ
  D_FF d_ff_26 (.D(E[1]), .C(CLK), .Q(S[1]));  // open: nQ
  D_FF d_ff_27 (.D(E[2]), .C(CLK), .Q(S[2]));  // open: nQ
  D_FF d_ff_28 (.D(E[3]), .C(CLK), .Q(S[3]));  // open: nQ
  D_FF d_ff_29 (.D(E[4]), .C(CLK), .Q(S[4]));  // open: nQ
  D_FF d_ff_30 (.D(E[5]), .C(CLK), .Q(S[5]));  // open: nQ
  D_FF d_ff_31 (.D(E[6]), .C(CLK), .Q(S[6]));  // open: nQ
  D_FF d_ff_32 (.D(E[7]), .C(CLK), .Q(S[7]));  // open: nQ
endmodule
