// Digital circuit SLT.dig as structural Verilog
module SLT (
  input  [31:0] RS1,
  input  [31:0] RS2,
  output [31:0] S
);

  wire and_1_out, and_2_out, not_1_out, xnor_1_out;
  wire [31:0] sub_1_s;

  SUB sub_1 (.RS1({RS1[30:0], RS1[31]}), .RS2({RS2[30:0], RS2[31]}), .S(sub_1_s));  // open: OF
  not not_1 (not_1_out, RS2[31]);
  xnor xnor_1 (xnor_1_out, RS1[31], RS2[31]);
  and and_1 (and_1_out, RS1[31], not_1_out);
  and and_2 (and_2_out, xnor_1_out, sub_1_s[31]);
  or or_1 (S[31], and_1_out, and_2_out);

  assign S[30:0] = {31{S[31]}};
endmodule
