// Digital circuit SUB.dig as structural Verilog
module SUB (
  input  [31:0] RS1,
  input  [31:0] RS2,
  output OF,
  output [31:0] S
);

  wire [31:0] add_1_s, not_1_out;

  assign not_1_out = ~RS2;  // Not not_1, 32 bits wide
  ADD add_1 (.RS1(not_1_out), .RS2(32'h1), .S(add_1_s));  // open: Cout
  ADD add_2 (.RS1(RS1), .RS2(add_1_s), .Cout(OF), .S(S));
endmodule
