// Digital circuit XOR.dig as structural Verilog
module XOR (
  input  [31:0] RS1,
  input  [31:0] RS2,
  output [31:0] S
);

  xor xor_1 (S[0], RS1[0], RS2[0]);
  xor xor_2 (S[1], RS1[1], RS2[1]);
  xor xor_3 (S[2], RS1[2], RS2[2]);
  xor xor_4 (S[3], RS1[3], RS2[3]);
  xor xor_5 (S[4], RS1[4], RS2[4]);
  xor xor_6 (S[5], RS1[5], RS2[5]);
  xor xor_7 (S[6], RS1[6], RS2[6]);
  xor xor_8 (S[7], RS1[7], RS2[7]);
  xor xor_9 (S[8], RS1[8], RS2[8]);
  xor xor_10 (S[9], RS1[9], RS2[9]);
  xor xor_11 (S[10], RS1[10], RS2[10]);
  xor xor_12 (S[11], RS1[11], RS2[11]);
  xor xor_13 (S[12], RS1[12], RS2[12]);
  xor xor_14 (S[13], RS1[13], RS2[13]);
  xor xor_15 (S[14], RS1[14], RS2[14]);
  xor xor_16 (S[15], RS1[15], RS2[15]);
  xor xor_17 (S[16], RS1[16], RS2[16]);
  xor xor_18 (S[17], RS1[17], RS2[17]);
  xor xor_19 (S[18], RS1[18], RS2[18]);
  xor xor_20 (S[19], RS1[19], RS2[19]);
  xor xor_21 (S[20], RS1[20], RS2[20]);
  xor xor_22 (S[21], RS1[21], RS2[21]);
  xor xor_23 (S[22], RS1[22], RS2[22]);
  xor xor_24 (S[23], RS1[23], RS2[23]);
  xor xor_25 (S[24], RS1[24], RS2[24]);
  xor xor_26 (S[25], RS1[25], RS2[25]);
  xor xor_27 (S[26], RS1[26], RS2[26]);
  xor xor_28 (S[27], RS1[27], RS2[27]);
  xor xor_29 (S[28], RS1[28], RS2[28]);
  xor xor_30 (S[29], RS1[29], RS2[29]);
  xor xor_31 (S[30], RS1[30], RS2[30]);
  xor xor_32 (S[31], RS1[31], RS2[31]);
endmodule
